# Fritzing sketch Attuatori (saved by Fritzing 0.7.4b)
breadboards: 1

parts:
  Arduino2 = Arduino
  Q2 = NPN-Transistor [package="TO92 [THT]"]
  R3 = Resistor [tolerance=±5% resistance=1k package=THT]
  S2 = Pushbutton [package="[THT]"]  # not connected
  R4 = Resistor [tolerance=±5% resistance=10k package=THT]
  LED1 = LED - 5mm [color="Red (633nm)" package="5 mm [THT]"]
  R5 = Rotary Potentiometer (Small) [maximum_resistance=100kΩ]
  J1 = Basic Servo
  R6 = Resistor [tolerance=±5% resistance=220 package=THT]
  S3 = Pushbutton [package="[THT]"]
  R7 = Resistor [tolerance=±5% resistance=10k package=THT]

nets:
  N1: Arduino2.D8, R3.Pin_0
  N2: Arduino2.D6, S3.Pin_1, S3.Pin_2
  N3: Arduino2.D5, R6.Pin_0
  N4: Arduino2.D3, J1.pulse
  N5: Arduino2.+5V, S3.Pin_3, S3.Pin_4
  N6: Arduino2.GND, Q2.E, R4.Pin_0, R7.Pin_0
  N7: Arduino2.A1, R5.wiper
  N8: Q2.C, R3.Pin_1
  N9: LED1.anode, R6.Pin_1

notes:
  ---VENTOLE---
  VERDE GND
  ROSSO Vcc
