# Fritzing sketch schema elettronico (saved by Fritzing 0.7.12b)
breadboards: 1

parts:
  Arduino1 = Arduino
  IC1 = L293D [package=THT]
  M1 = DC Motor
  LED2 = LED - 3mm [color="Red (633nm)" package="3 mm [THT]"]
  R1 = Resistor [tolerance=±5% resistance=10k package=THT]
  R2 = Resistor [tolerance=±5% resistance=10k package=THT]
  R3 = Resistor [tolerance=±5% resistance=10k package=THT]
  LED3 = LED - 3mm [color="Red (633nm)" package="3 mm [THT]"]
  LED4 = LED - 3mm [color="Red (633nm)" package="3 mm [THT]"]
  M2 = DC Motor
  LED5 = LED - 3mm [color="Red (633nm)" package="3 mm [THT]"]
  LED6 = LED - 3mm [color="Red (633nm)" package="3 mm [THT]"]
  R4 = Resistor [tolerance=±5% resistance=10k package=THT]
  R5 = Resistor [tolerance=±5% resistance=10k package=THT]

nets:
  N1: Arduino1.D11, IC1.In_3
  N2: Arduino1.D10, IC1.In_1
  N3: Arduino1.D9, R4.Pin_0
  N4: Arduino1.D8, R1.Pin_0
  N5: Arduino1.D5, R3.Pin_0
  N6: Arduino1.D4, R2.Pin_0
  N7: Arduino1.D3, R5.Pin_0
  N8: IC1.Enable_1, IC1.+Vmotor, IC1.Enable_2, IC1.+V
  N9: IC1.Out_1_(_Controlled_by_Enable_1_), M1.pin_1
  N10: IC1.0V, LED2.anode, LED3.anode, LED4.anode, LED5.anode, LED6.anode
  N11: IC1.Out_2_(_Controlled_by_Enable_1_), M1.pin_2
  N12: IC1.Out_3_(_Controlled_by_Enable_2_), M2.pin_2
  N13: IC1.Out_4_(_Controlled_by_Enable_2_), M2.pin_1
  N14: LED2.cathode, R2.Pin_1
  N15: R1.Pin_1, LED3.cathode
  N16: R3.Pin_1, LED4.cathode
  N17: LED5.cathode, R5.Pin_1
  N18: LED6.cathode, R4.Pin_1
