# Fritzing sketch sequenzled (saved by Fritzing 0.7.4b)
breadboards: 1

parts:
  Arduino_Ethernet_Shield1 = Arduino Ethernet Shield
  R1 = Resistor [tolerance=±5% resistance=220 package=THT]
  R2 = Resistor [tolerance=±5% resistance=220 package=THT]
  R3 = Resistor [tolerance=±5% resistance=220 package=THT]
  R4 = Resistor [tolerance=±5% resistance=220 package=THT]
  R5 = Resistor [tolerance=±5% resistance=220 package=THT]
  R6 = Resistor [tolerance=±5% resistance=220 package=THT]
  LED1 = LED - 5mm [color="Red (633nm)" package="5 mm [THT]"]
  LED2 = LED - 5mm [color="Red (633nm)" package="5 mm [THT]"]
  LED3 = LED - 5mm [color="Red (633nm)" package="5 mm [THT]"]
  LED4 = LED - 5mm [color="Red (633nm)" package="5 mm [THT]"]
  LED5 = LED - 5mm [color="Red (633nm)" package="5 mm [THT]"]
  LED6 = LED - 5mm [color="Red (633nm)" package="5 mm [THT]"]

nets:
  N1: Arduino_Ethernet_Shield1.GND, LED1.cathode, LED2.cathode, LED3.cathode, LED4.cathode, LED5.cathode, LED6.cathode
  N2: Arduino_Ethernet_Shield1.D7, R1.Pin_0
  N3: Arduino_Ethernet_Shield1.D6, R2.Pin_0
  N4: Arduino_Ethernet_Shield1.D5, R3.Pin_0
  N5: Arduino_Ethernet_Shield1.SS, R4.Pin_0
  N6: Arduino_Ethernet_Shield1.D3, R5.Pin_0
  N7: Arduino_Ethernet_Shield1.D2, R6.Pin_0
  N8: R1.Pin_1, LED1.anode
  N9: R2.Pin_1, LED2.anode
  N10: R3.Pin_1, LED3.anode
  N11: R4.Pin_1, LED4.anode
  N12: R5.Pin_1, LED5.anode
  N13: R6.Pin_1, LED6.anode
