# Fritzing sketch setLedFromWeb (saved by Fritzing 0.7.4b)
breadboards: 1

parts:
  Arduino_Ethernet_Shield1 = Arduino Ethernet Shield
  R1 = Resistor [tolerance=±5% resistance=220 package=THT]
  LED1 = LED - 5mm [color="Red (633nm)" package="5 mm [THT]"]

nets:
  N1: Arduino_Ethernet_Shield1.GND, LED1.cathode
  N2: Arduino_Ethernet_Shield1.D6, R1.Pin_0
  N3: R1.Pin_1, LED1.anode
