# Fritzing sketch lightSensorScheme (saved by Fritzing 0.7.4b)
breadboards: 1

parts:
  C1 = Ceramic Capacitor [capacitance=100nF package="100 mil [THT, multilayer]"]
  Arduino1 = Arduino

nets:
  N1: C1.0, Arduino1.+5V
  N2: C1.1, Arduino1.A0

notes:
  BIANCO: Vin
  NERO: GROUND
  ROSSO: 5v
