# Fritzing sketch RFID_lettura (saved by Fritzing 0.7.4b)
breadboards: 1

parts:
  Arduino1 = Arduino
  LED1 = RGB LED (com. anode, rbg) [package="5 mm [THT]"]
  R1 = Resistor [tolerance=±5% resistance=220 package=THT]
  R2 = Resistor [tolerance=±5% resistance=220 package=THT]
  R3 = Resistor [tolerance=±5% resistance=220 package=THT]  # not connected
  RFID_Evaluation_Shield1 = RFID  # not connected

nets:
  N1: Arduino1.D5, R2.Pin_0
  N2: Arduino1.D3, R1.Pin_0
  N3: Arduino1.+5V, LED1.common_anode
  N4: LED1.red_cathode, R1.Pin_1
  N5: LED1.blue_cathode, R2.Pin_1

notes:
  RFID module = SM130
  Bisogna saldare i componenti sulla shield qua a fianco (modulo e pin) e poi basta attaccarla ad Arduino
  Pin 7 e 8 usati per la comunicazione con la shield
