# Fritzing sketch stazione_meteo (saved by Fritzing 0.7.4b)
breadboards: 1

parts:
  Arduino1 = Arduino
  RHT2 = Humidity and Temperature Sensor RHT03
  R2 = Resistor [tolerance=±5% resistance=1k package=THT]
  C1 = Ceramic Capacitor [capacitance=100nF package="100 mil [THT, multilayer]"]
  C2 = Ceramic Capacitor [capacitance=100nF package="100 mil [THT, multilayer]"]
  R3 = Resistor [tolerance=±5% resistance=220 package=THT]
  R4 = Resistor [tolerance=±5% resistance=220 package=THT]
  R5 = Resistor [tolerance=±5% resistance=220 package=THT]
  R6 = Resistor [tolerance=±5% resistance=220 package=THT]
  LED1 = LED - 5mm [color="Green (560nm)" package="5 mm [THT]"]
  LED2 = LED - 5mm [color="Green (560nm)" package="5 mm [THT]"]
  LED3 = LED - 5mm [color="Green (560nm)" package="5 mm [THT]"]
  LED4 = LED - 5mm [color="Green (560nm)" package="5 mm [THT]"]
  Part1 = Arduino Wireless SD Shield  # not connected

nets:
  N1: Arduino1.D8, RHT2.Data-signal, R2.Pin_1
  N2: Arduino1.D5, R3.Pin_1
  N3: Arduino1.D4, R4.Pin_1
  N4: Arduino1.D3, R5.Pin_1
  N5: Arduino1.D2, R6.Pin_1
  N6: Arduino1.A0, C1.1
  N7: Arduino1.A1, C2.1
  N8: RHT2.Vcc, R2.Pin_0
  N9: RHT2.GND_2, LED1.cathode, LED2.cathode, LED3.cathode, LED4.cathode
  N10: C1.0, C2.0
  N11: R3.Pin_0, LED1.anode
  N12: R4.Pin_0, LED2.anode
  N13: R5.Pin_0, LED3.anode
  N14: R6.Pin_0, LED4.anode

notes:
  SOUND SENSOR
  BIANCO: Vin
  NERO: GROUND
  ROSSO: 5v
  LIGHT SENSOR
  BIANCO: Vin
  NERO: GROUND
  ROSSO: 5v
  SMOKE SENSOR
  B-H-B -> RED (V+)
  A-H-> BLACK (GND)
  A-> YELLOW (SOURCE)
