# Fritzing sketch xBeeTX&RX (saved by Fritzing 0.7.4b)
breadboards: 1

parts:
  U1 = XBee  # not connected
  Part1 = Arduino Wireless SD Shield
  S2 = Pushbutton [package="[THT]"]
  R3 = Resistor [tolerance=±5% resistance=330 package=THT]
  R4 = Resistor [tolerance=±5% resistance=10k package=THT]
  LED3 = LED - 5mm [color="Red (633nm)" package="5 mm [THT]"]
  Part2 = Arduino Wireless SD Shield
  U2 = XBee  # not connected

nets:
  N1: Part1.D2, S2.Pin_1, S2.Pin_2, R4.Pin_0
  N2: Part1.+5V, S2.Pin_3, S2.Pin_4
  N3: Part1.GND, R4.Pin_1
  N4: R3.Pin_0, Part2.D2
  N5: R3.Pin_1, LED3.cathode
